# Fritzing sketch PiLOG NRF24 I2C (saved by Fritzing 0.9.3b)
circuit board: 2.8cm x 3.2cm
breadboards: 1

parts:
  NRF24 = NRF24L01+ Breakout Board
  C1 = Electrolytic Capacitor [capacitance=1µF package="100 mil [THT, electrolytic]"]
  U1 = ATTINY45 [package=dip]
  R1 = Resistor [tolerance=±5% resistance=10k package=THT]
  R2 = Resistor [tolerance=±5% resistance=4.7k package=THT]
  R3 = Resistor [tolerance=±5% resistance=1k package=THT]
  C2 = Ceramic Capacitor [capacitance=100nF package="100 mil [THT, multilayer]"]
  R4 = Resistor [tolerance=±5% resistance=4.7k package=THT]
  J2 = double row female pin header, 20 pins [form="♀ (female)" part_number="PC104 20 Pin 2x10"]
  R5 = Resistor [tolerance=±5% resistance=4.7k package=THT]

nets:
  GND: NRF24.GND, C1.-, U1.GND, C2.1, J2.pin15
  VCC: NRF24.VCC, C1.+, U1.VCC, R1.Pin_0, R4.Pin_0, J2.pin11, J2.pin19, R5.Pin_0
  N1: NRF24.CE, NRF24.CS, R3.Pin_0, C2.0
  N2: NRF24.SCK, U1.PB3(ADC3), R3.Pin_1
  N3: NRF24.MOSI, U1.PB4(ADC2), R2.Pin_0
  N4: NRF24.MISO, R2.Pin_1
  N5: U1.PB5(NRES), R1.Pin_1
  N6: U1.PB0(MOSI), R4.Pin_1, J2.pin12
  N7: U1.PB2(SCK_ADC1), J2.pin13, R5.Pin_1

notes:
  PiLOG
  NRF24 Bridge
  by GJ
